# Fritzing sketch wiringTwoSCD41ToArduinoUnoR4 (saved by Fritzing 1.0.4)
breadboards: 1

parts:
  A1 = Arduino UNO R4 WiFi
  SCD41_B = Adafruit SCD4x [part_number="Adafruit #5187"]
  SCD41_A_(Sensirion_SEK) = polarizedheader 4pin 0.156in [package=THT]
  R1 = Resistor [tolerance=±5% power=0.25W resistance=220 package=THT]
  R2 = Resistor [tolerance=±5% power=0.25W resistance=220 package=THT]

nets:
  N1: A1.Pin_7, A1.Pin_19, SCD41_B.VCC, SCD41_A_(Sensirion_SEK).pin3, R1.Pin_1, R2.Pin_1
  N2: A1.Pin_9, A1.Pin_18, SCD41_B.GND, SCD41_A_(Sensirion_SEK).pin2
  N3: A1.Pin_20, SCD41_B.SDA
  N4: A1.Pin_21, SCD41_B.SCL
  N5: A1.Pin_50, SCD41_A_(Sensirion_SEK).pin4, R2.Pin_0
  N6: A1.Pin_51, SCD41_A_(Sensirion_SEK).pin1, R1.Pin_0

custom parts:
  Arduino UNO R4 WiFi: The Arduino UNO R4 WiFi merges the RA4M1 microprocessor from Renesas with the ESP32-S3 from Espressif, creating an all-in-one tool for makers with enhanced processing power and a diverse array of new peripherals.
  Adafruit SCD4x: Take a deep breath in...now slowly breathe out. Mmm isn't it wonderful? All that air around us, which we bring into our lungs, extracts oxygen from and then breathes out carbon dioxide. CO2 is essential for life on this planet we call Earth - we and plants take turns using and emitting CO2 in an elegant symbiosis. But it's important to keep that CO2 balanced - you don't want too much around,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
