# Fritzing sketch wiringTwoSCD41ToESP (saved by Fritzing 1.0.4)

parts:
  U1 = ESP32-38PinWide [part_number=ESP32-38PinWide]
  H1 = polarizedheader 4pin 0.156in [package=THT]
  H2 = polarizedheader 4pin 0.156in [package=THT]

nets:
  N1: U1.3.3, H1.pin3
  N2: U1.GND, H1.pin2, H2.pin2
  N3: U1.VIN, H2.pin3
  N4: U1.GPIO16, H2.pin4
  N5: U1.GPIO17, H2.pin1
  N6: U1.GPIO21, U1.GPIO3, H1.pin4
  N7: U1.GPIO22, U1.GPIO23, H1.pin1

custom parts:
  ESP32-38PinWide: Generic 38-Pin ESP32 with wide format (only access to one side of pins on a breadboard) based on Stephen Lilley's HiLetgo ESP-WROOM-32 ESP32 ESP-32S Development Board.
