# Fritzing sketch wiringTwoSCD41ToSTM32Nucleo64 (saved by Fritzing 1.0.4)
breadboards: 1

parts:
  SCD41_-_B = polarizedheader 4pin 0.156in [package=THT]
  SCD41_-_A = polarizedheader 4pin 0.156in [package=THT]
  R1 = Resistor [tolerance=±5% power=0.25W resistance=2.2k package=THT]
  R2 = Resistor [tolerance=±5% power=0.25W resistance=2.2k package=THT]
  R3 = Resistor [tolerance=±5% power=0.25W resistance=2.2k package=THT]
  R4 = Resistor [tolerance=±5% power=0.25W resistance=2.2k package=THT]
  J1 = STM32 Nucleo boards

nets:
  N1: SCD41_-_B.pin1, R2.Pin_1, J1.D6_PWM
  N2: SCD41_-_B.pin2, SCD41_-_A.pin2, J1.GND
  N3: SCD41_-_B.pin3, SCD41_-_A.pin3, R1.Pin_0, R2.Pin_0, R3.Pin_0, R4.Pin_0, J1.3V3
  N4: SCD41_-_B.pin4, R3.Pin_1, J1.D3_PWM
  N5: SCD41_-_A.pin1, R1.Pin_1, J1.A5/SCL
  N6: SCD41_-_A.pin4, R4.Pin_1, J1.A4/SDA
